# Fritzing sketch pi-pico-neopixel (saved by Fritzing 0.9.6b)
breadboards: 1

parts:
  A1 = Raspberry Pi Pico H
  S1 = Momentary Switch [package=tactile-pth]
  Part1 = NeoPixel Stick [part_number=1426]  # not connected
  C1 = Capacitor [package=cap-pth-small2]
  C2 = Capacitor [package=cap-pth-small2]
  C3 = Capacitor [package=cap-pth-small2]

nets:
  N1: A1.GND, S1.2, C1.1
  N2: A1.GP19, C1.2, C2.2, C3.1
  N3: A1.RUN, S1.3
  N4: A1.VBUS, C2.1

custom parts:
  Raspberry Pi Pico H: Raspberry Pi Pico H. Based around the RP2040 microcontroller the Pico H is a low cost microcontroller device bringing Raspberry Pi quality, cost, and easy of use to the microcontroller space.
  NeoPixel Stick: Make your own little LED strip arrangement with this stick of NeoPixel LEDs. We crammed 8 of the tiny 5050 (5mm x 5mm) smart RGB LEDs onto a PCB with mounting holes and a chainable design. Use only one microcontroller pin to control as many as you can chain together! Each LED is addressable as the driver chip is inside the LED. Each one has ~18mA constant current drive so the color will be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
